# Fritzing sketch ESP-GoProRemote (saved by Fritzing 0.9.3b)

parts:
  U1 = ESP8266 WiFi Module [part_number=ESP8266]
  S1 = Pushbutton [package="[THT]"]
  R1 = Resistor [tolerance=±5% resistance=220 package=THT]
  JP1 = Header 2 [package=jst-2-pth]
  U3 = V_REG_LD1117VXX [package=78xxl]
  R2 = Resistor [tolerance=±5% resistance=10k package=THT]
  LED = LED - 3mm [color="Blue (470nm)" package="3 mm [THT]"]

nets:
  N1: U1.VCC, U3.OUT, R2.Pin_0, LED.anode
  N2: U1.GPIO_0, R1.Pin_1
  N3: U1.GPIO_2, S1.Pin_1, S1.Pin_2
  N4: U1.CH_PD, R2.Pin_1
  GND: U1.GND, S1.Pin_3, S1.Pin_4, JP1.1, U3.GND
  N5: R1.Pin_0, LED.cathode
  N6: JP1.2, U3.IN

custom parts:
  ESP8266 WiFi Module: Generic WiFi Module based on the ESP8266 with onboard PCB antenna and UART communications
